# Fritzing sketch electrical_schematic (saved by Fritzing 0.9.4)
breadboards: 1

parts:
  Raspberry_Pi_5_8GB = Raspberry Pi B+
  MCP3008 = MCP3008 [package=dil16]
  IR1 = TSOP312.., 314.. [package=THT]
  INA1 = INA219 DC Current Sensor Breakout
  RFID = RFID-RC522-v2
  LED1 = LEDs [package=led10mm]
  LED2 = LEDs [package=led10mm]
  LED4 = LEDs [package=led10mm]
  LED_3 = LEDs [package=led10mm]
  M1 = DC Motor
  INA2 = INA219 DC Current Sensor Breakout
  INA3 = INA219 DC Current Sensor Breakout
  INA4 = INA219 DC Current Sensor Breakout
  R7/Heating_pad = Resistor [tolerance=±5% resistance=10 package="2512 [SMD]"]
  Q1_SS8050 = TRANSISTOR_NPN [package=to-92]
  Q2_SS8050 = TRANSISTOR_NPN [package=to-92]
  R6 = Resistor [tolerance=±5% resistance=470 package="2512 [SMD]"]
  R5 = Resistor [tolerance=±5% resistance=470 package="2512 [SMD]"]
  R1 = Resistor [tolerance=±5% resistance=100 package="0805 [SMD]"]
  R3 = Resistor [tolerance=±5% resistance=100 package="0805 [SMD]"]
  R2 = Resistor [tolerance=±5% resistance=100 package="0805 [SMD]"]
  D1 = Rectifier Diode [package="Melf DO-213 AA [SMD]"]
  R8/Heating_pad = Resistor [tolerance=±5% resistance=10 package="2512 [SMD]"]
  R4 = Resistor [tolerance=±5% resistance=100 package="0805 [SMD]"]
  Q3_2N2222A = TRANSISTOR_NPN [package=to-92]
  Q4_2N2222A = TRANSISTOR_NPN [package=to-92]
  R9 = Resistor [tolerance=±5% resistance=2k package="2512 [SMD]"]
  R10 = Resistor [tolerance=±5% resistance=2k package="2512 [SMD]"]
  Q5_2N2222A = TRANSISTOR_NPN [package=to-92]
  R11 = Resistor [tolerance=±5% resistance=5.1k package="2512 [SMD]"]
  L1_SOLENOIDE_LOCK = Solenoid
  D3 = Rectifier Diode [package="Melf DO-213 AA [SMD]"]
  Q5_TIP120 = TRANSISTOR_NPN [package=to-92]
  R12 = Resistor [tolerance=±5% resistance=470k package="2512 [SMD]"]
  S2 = Momentary Switch [package=tactile_switch_smd]
  DS1 = DS18B20 1-Wire Temperature Sensor [part_number=DS18B20]
  R14 = Resistor [tolerance=±5% resistance=4.7k package="0805 [SMD]"]
  S3 = TILT-SWITCH-SW-200D [package=reed_switch_plastic]
  R15 = Resistor [tolerance=±5% resistance=470 package="0805 [SMD]"]
  R16 = Resistor [tolerance=±5% resistance=470 package="0805 [SMD]"]
  U1 = PCF8574 [package="DIP16 [THT]"]
  U2 = LCD-16X2 [package=lcd-8x2]
  R17 = Photocell (LDR) [package=THT]
  R18 = Trimmer Potentiometer [maximum_resistance=10kΩ package=THT]
  R19 = Resistor [tolerance=±5% resistance=10k package="0805 [SMD]"]
  R20 = Trimmer Potentiometer [maximum_resistance=10kΩ package=THT]
  LED_4 = LEDs [package=led10mm]
  LED6 = LEDs [package=led10mm]
  R22 = Resistor [tolerance=±5% resistance=100 package="0805 [SMD]"]
  R23 = Resistor [tolerance=±5% resistance=100 package="0805 [SMD]"]
  U4 = Mini-360 DC-DC Buck converter [package=THT]
  Part5 = Adafruit TCA9548A
  U5 = Mini-360 DC-DC Buck converter [package=THT]
  D5 = Rectifier Diode [package="Melf DO-213 AA [SMD]"]
  INA8 = INA219 DC Current Sensor Breakout
  INA9 = INA219 DC Current Sensor Breakout
  Solar_panel1 = SOLAR-IXYS [package=solarbit-12x1]
  Powerbank_INPUT_5V1 = BC9VPC [package=bc9vpc]
  Resistors = Resistor [tolerance=±5% resistance=4.7k package="2010 [SMD]"]
  All_resistors2 = Resistor [tolerance=±5% resistance=4.7k package="2010 [SMD]"]
  Powerbank_OUTPUT_5V1 = BC9VPC [package=bc9vpc]
  S4 = Momentary Switch [package=tactile_switch_smd]
  R36 = Resistor [tolerance=±5% resistance=470 package="0805 [SMD]"]

nets:
  N1: Raspberry_Pi_5_8GB.GPIO2, U1.SDA, Part5.INPUTSDA, Resistors.Pin_1
  N2: Raspberry_Pi_5_8GB.GPIO3, U1.SCL, Part5.INPUTSCL, All_resistors2.Pin_1
  N3: Raspberry_Pi_5_8GB.GPIO4, DS1.DQ, R14.Pin_0
  GND: Raspberry_Pi_5_8GB.GND, U4.IN-, U4.OUT-, Part5.GND, Part5.A0, Part5.A1, Part5.A2, INA8.GND, INA9.GND, Powerbank_OUTPUT_5V1.V-
  N4: Raspberry_Pi_5_8GB.GPIO27, S4.3, R36.Pin_1
  N5: Raspberry_Pi_5_8GB.GPIO22, S3.2, R15.Pin_1
  N6: Raspberry_Pi_5_8GB.GPIO10, RFID.MOSI
  N7: Raspberry_Pi_5_8GB.GPIO9, RFID.MISO
  N8: Raspberry_Pi_5_8GB.GPIO11, RFID.SCK
  N9: Raspberry_Pi_5_8GB.GPIO5, U2.E
  N10: Raspberry_Pi_5_8GB.GPIO6, U2.RS
  N11: Raspberry_Pi_5_8GB.GPIO13, S2.3, R16.Pin_1
  N12: Raspberry_Pi_5_8GB.GPIO19, MCP3008.Din
  N13: Raspberry_Pi_5_8GB.GPIO26, IR1.Data
  N14: Raspberry_Pi_5_8GB.GPIO21, MCP3008.CLK
  N15: Raspberry_Pi_5_8GB.GPIO20, MCP3008.Dout
  N16: Raspberry_Pi_5_8GB.GPIO16, R6.Pin_0
  N17: Raspberry_Pi_5_8GB.GPIO12, R5.Pin_0
  N18: Raspberry_Pi_5_8GB.GPIO8, RFID.SDA
  N19: Raspberry_Pi_5_8GB.GPIO25, R10.Pin_0
  N20: Raspberry_Pi_5_8GB.GPIO24, R9.Pin_0
  N21: Raspberry_Pi_5_8GB.GPIO23, RFID.GND
  N22: Raspberry_Pi_5_8GB.GPIO18, MCP3008.CS/SHDN
  N23: Raspberry_Pi_5_8GB.GPIO15, R12.Pin_0
  N24: Raspberry_Pi_5_8GB.GPIO14, R11.Pin_0
  N25: MCP3008.CH0, R17.pin_0, R19.Pin_1
  N26: MCP3008.CH1, R18.wiper
  GND_2: MCP3008.DGND, MCP3008.AGND, IR1.GND, INA1.GND, RFID.RST, INA2.GND, Q1_SS8050.E, Q2_SS8050.E, Q3_2N2222A.E, Q4_2N2222A.E, Q5_2N2222A.E, Q5_TIP120.E, S2.1, DS1.GND, S3.1, U1.A0, U1.A1, U1.A2, U1.GND, U2.VSS, U2.R_W, U2.K, R17.pin_1, R18.leg2, R20.leg1, S4.1
  VCC: MCP3008.VREF, MCP3008.VDD, INA1.VCC, INA1.Vin+, RFID.3.3V, INA2.VCC, INA2.Vin+, INA3.VCC, INA4.VCC, DS1.VDD, R14.Pin_1, R15.Pin_0, R16.Pin_0, U1.VCC, R18.leg1, R19.Pin_0, Part5.VCC, INA8.VCC, INA9.VCC, Resistors.Pin_0, All_resistors2.Pin_0, R36.Pin_0
  N27: IR1.Vs, U2.VDD, U2.A, R20.leg2, U4.IN+, INA8.Vin-
  N28: INA1.SCL, Part5.7SCL
  N29: INA1.SDA, Part5.7SDA
  N30: INA1.Vin-, LED1.A, LED2.A
  N31: LED1.C, R1.Pin_0
  N32: LED2.C, R2.Pin_0
  N33: LED4.C, R3.Pin_0
  N34: LED4.A, LED_3.A, INA2.Vin-
  N35: LED_3.C, R4.Pin_0
  N36: M1.pin_1, INA3.Vin-, D1.cathode
  N37: M1.pin_2, Q1_SS8050.C, D1.anode
  N38: INA2.SCL, Part5.6SCL
  N39: INA2.SDA, Part5.6SDA
  GND_3: INA3.GND, INA4.GND
  N40: INA3.SCL, Part5.5SCL
  N41: INA3.SDA, Part5.5SDA
  N42: INA3.Vin+, INA4.Vin+, L1_SOLENOIDE_LOCK.pin1, D3.cathode, LED_4.A, LED6.A
  N43: INA4.SCL, Part5.4SCL
  N44: INA4.SDA, Part5.4SDA
  N45: INA4.Vin-, R7/Heating_pad.Pin_0, R8/Heating_pad.Pin_0
  N46: R7/Heating_pad.Pin_1, Q2_SS8050.C, R8/Heating_pad.Pin_1
  N47: Q1_SS8050.B, R5.Pin_1
  N48: Q2_SS8050.B, R6.Pin_1
  N49: R1.Pin_1, R2.Pin_1, Q4_2N2222A.C
  N50: R3.Pin_1, R4.Pin_1, Q3_2N2222A.C
  N51: Q3_2N2222A.B, R10.Pin_1
  N52: Q4_2N2222A.B, R9.Pin_1
  N53: Q5_2N2222A.B, R11.Pin_1
  N54: Q5_2N2222A.C, R22.Pin_1, R23.Pin_1
  N55: L1_SOLENOIDE_LOCK.pin2, D3.anode, Q5_TIP120.C
  N56: Q5_TIP120.B, R12.Pin_1
  N57: U1.P0, U2.DB0
  N58: U1.P1, U2.DB1
  N59: U1.P2, U2.DB2
  N60: U1.P3, U2.DB3
  N61: U1.P4, U2.DB4
  N62: U1.P5, U2.DB5
  N63: U1.P6, U2.DB6
  N64: U1.P7, U2.DB7
  N65: U2.VO, R20.wiper
  N66: LED_4.C, R23.Pin_0
  N67: LED6.C, R22.Pin_0
  N68: Part5.2SDA, INA9.SDA
  N69: Part5.2SCL, INA9.SCL
  N70: Part5.3SDA, INA8.SDA
  N71: Part5.3SCL, INA8.SCL
  N72: U5.IN-, Solar_panel1.A
  N73: U5.IN+, D5.cathode
  N74: U5.OUT+, INA9.Vin+
  N75: U5.OUT-, Powerbank_INPUT_5V1.V-
  N76: D5.anode, Solar_panel1.C
  N77: INA8.Vin+, Powerbank_OUTPUT_5V1.V+
  N78: INA9.Vin-, Powerbank_INPUT_5V1.V+

custom parts:
  INA219 DC Current Sensor Breakout: INA DC Current Sensor Breakout
  RFID-RC522-v2: A simple China made RFID-RC522 Reader; do check the pin labels, as this is a MFRC522 based clone.
  Mini-360 DC-DC Buck converter: Mini-360 DC-DC Buck converter. Tiny buck step down voltage converter, input voltage 4.75 to 23V output 1 to 17V adjustable. Available from ebay and the like.
  Adafruit TCA9548A: You just found the perfect I2C sensor, and you want to wire up two or three or more of them to your Arduino when you realize "Uh oh, this chip has a fixed I2C address, and from what I know about I2C, you cannot have two devices with the same address on the same SDA/SCL pins!" Are you out of luck? You would be, if you didn't have this ultra-cool TCA9548A 1-to-8 I2C multiplexer! Finally, a way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
