# Fritzing sketch schematic (saved by Fritzing 0.9.4)
breadboards: 1

parts:
  Raspberry_Pi_5_8GB = Raspberry Pi B+
  MCP3008 = MCP3008 [package=dil16]
  IR1 = TSOP312.., 314.. [package=THT]
  D2 = SOLAR-IXYS [package=solarbit-12x1]  # not connected
  Battery_5V = BC9VPC [package=bc9vpc]
  INA1 = INA219 DC Current Sensor Breakout
  RFID = RFID-RC522-v2
  LED1 = LEDs [package=led10mm]
  LED2 = LEDs [package=led10mm]
  LED4 = LEDs [package=led10mm]
  LED_3 = LEDs [package=led10mm]
  M1 = DC Motor
  LED5 = LEDs [package=led10mm]
  INA2 = INA219 DC Current Sensor Breakout
  INA3 = INA219 DC Current Sensor Breakout
  INA4 = INA219 DC Current Sensor Breakout
  R7/Heating_pad = Resistor [tolerance=±5% resistance=10 package="2512 [SMD]"]
  Q1_SS8050 = TRANSISTOR_NPN [package=to-92]
  Q2_SS8050 = TRANSISTOR_NPN [package=to-92]
  5V_TO_3V3 = Transformer [package=transformer_smd]
  R6 = Resistor [tolerance=±5% resistance=470 package="2512 [SMD]"]
  R5 = Resistor [tolerance=±5% resistance=470 package="2512 [SMD]"]
  R1 = Resistor [tolerance=±5% resistance=100 package="0805 [SMD]"]
  R3 = Resistor [tolerance=±5% resistance=100 package="0805 [SMD]"]
  R2 = Resistor [tolerance=±5% resistance=100 package="0805 [SMD]"]
  D1 = Rectifier Diode [package="Melf DO-213 AA [SMD]"]
  R8/Heating_pad = Resistor [tolerance=±5% resistance=10 package="2512 [SMD]"]
  R4 = Resistor [tolerance=±5% resistance=100 package="0805 [SMD]"]
  Q3_2N2222A = TRANSISTOR_NPN [package=to-92]
  Q4_2N2222A = TRANSISTOR_NPN [package=to-92]
  R9 = Resistor [tolerance=±5% resistance=2k package="2512 [SMD]"]
  R10 = Resistor [tolerance=±5% resistance=2k package="2512 [SMD]"]
  Q5_2N2222A = TRANSISTOR_NPN [package=to-92]
  R11 = Resistor [tolerance=±5% resistance=5.1k package="2512 [SMD]"]
  L1_SOLENOIDE_LOCK = Solenoid
  D3 = Rectifier Diode [package="Melf DO-213 AA [SMD]"]
  Q5_TIP120 = TRANSISTOR_NPN [package=to-92]
  R12 = Resistor [tolerance=±5% resistance=470k package="2512 [SMD]"]
  S2 = Momentary Switch [package=tactile_switch_smd]
  DS1 = DS18B20 1-Wire Temperature Sensor [part_number=DS18B20]
  R14 = Resistor [tolerance=±5% resistance=4.7k package="0805 [SMD]"]
  S3 = TILT-SWITCH-SW-200D [package=reed_switch_plastic]
  R15 = Resistor [tolerance=±5% resistance=470 package="0805 [SMD]"]
  R16 = Resistor [tolerance=±5% resistance=470 package="0805 [SMD]"]
  U1 = PCF8574 [package="DIP16 [THT]"]  # not connected
  U2 = LCD-16X2 [package=lcd-8x2]  # not connected
  R17 = Photocell (LDR) [package=THT]
  R18 = Trimmer Potentiometer [maximum_resistance=10kΩ package=THT]
  R19 = Resistor [tolerance=±5% resistance=10k package="0805 [SMD]"]

nets:
  N1: Raspberry_Pi_5_8GB.GPIO2, INA1.SDA, INA2.SDA, INA3.SDA, INA4.SDA
  N2: Raspberry_Pi_5_8GB.GPIO3, INA1.SCL, INA2.SCL, INA3.SCL, INA4.SCL
  N3: Raspberry_Pi_5_8GB.GPIO4, DS1.DQ, R14.Pin_0
  N4: Raspberry_Pi_5_8GB.GPIO10, MCP3008.Din, RFID.MOSI
  N5: Raspberry_Pi_5_8GB.GPIO9, MCP3008.Dout, RFID.MISO
  N6: Raspberry_Pi_5_8GB.GPIO11, MCP3008.CLK, RFID.SCK
  GND: Raspberry_Pi_5_8GB.GND, Battery_5V.V-, 5V_TO_3V3.1, 5V_TO_3V3.4
  N7: Raspberry_Pi_5_8GB.GPIO13, S3.2, R15.Pin_1
  N8: Raspberry_Pi_5_8GB.GPIO19, S2.3, R16.Pin_1
  N9: Raspberry_Pi_5_8GB.GPIO26, IR1.Data
  N10: Raspberry_Pi_5_8GB.GPIO21, R12.Pin_0
  N11: Raspberry_Pi_5_8GB.GPIO20, R11.Pin_0
  N12: Raspberry_Pi_5_8GB.GPIO16, R6.Pin_0
  N13: Raspberry_Pi_5_8GB.GPIO12, R5.Pin_0
  N14: Raspberry_Pi_5_8GB.GPIO7, RFID.SDA
  N15: Raspberry_Pi_5_8GB.GPIO8, MCP3008.CS/SHDN
  N16: Raspberry_Pi_5_8GB.GPIO25, R10.Pin_0
  N17: Raspberry_Pi_5_8GB.GPIO24, R9.Pin_0
  N18: MCP3008.CH0, R17.pin_0, R19.Pin_1
  N19: MCP3008.CH1, R18.wiper
  GND_2: MCP3008.DGND, MCP3008.AGND, IR1.GND, INA1.GND, RFID.RST, INA2.GND, INA3.GND, INA4.GND, Q2_SS8050.E, S2.1, DS1.GND, S3.1, R17.pin_1, R18.leg2
  VCC: MCP3008.VREF, MCP3008.VDD, INA1.VCC, INA1.Vin+, RFID.3.3V, LED5.A, INA2.VCC, INA2.Vin+, INA3.VCC, INA4.VCC, 5V_TO_3V3.2, DS1.VDD, R14.Pin_1, R15.Pin_0, R16.Pin_0, R18.leg1, R19.Pin_0
  N20: IR1.Vs, Battery_5V.V+, INA3.Vin+, INA4.Vin+, 5V_TO_3V3.3, L1_SOLENOIDE_LOCK.pin1, D3.cathode
  N21: LED1.C, R1.Pin_0
  N22: LED1.A, LED2.A
  N23: LED2.C, R2.Pin_0
  N24: LED4.C, R3.Pin_0
  N25: LED4.A, LED_3.A, INA2.Vin-
  N26: LED_3.C, R4.Pin_0
  N27: M1.pin_1, D1.cathode
  N28: M1.pin_2, Q1_SS8050.C, D1.anode
  N29: LED5.C, Q5_2N2222A.C
  N30: INA4.Vin-, R7/Heating_pad.Pin_0, R8/Heating_pad.Pin_0
  N31: R7/Heating_pad.Pin_1, Q2_SS8050.C, R8/Heating_pad.Pin_1
  N32: Q1_SS8050.E, Q3_2N2222A.E, Q4_2N2222A.E, Q5_2N2222A.E, Q5_TIP120.E
  N33: Q1_SS8050.B, R5.Pin_1
  N34: Q2_SS8050.B, R6.Pin_1
  N35: R1.Pin_1, R2.Pin_1, Q4_2N2222A.C
  N36: R3.Pin_1, R4.Pin_1, Q3_2N2222A.C
  N37: Q3_2N2222A.B, R10.Pin_1
  N38: Q4_2N2222A.B, R9.Pin_1
  N39: Q5_2N2222A.B, R11.Pin_1
  N40: L1_SOLENOIDE_LOCK.pin2, D3.anode, Q5_TIP120.C
  N41: Q5_TIP120.B, R12.Pin_1

custom parts:
  INA219 DC Current Sensor Breakout: INA DC Current Sensor Breakout
  RFID-RC522-v2: A simple China made RFID-RC522 Reader; do check the pin labels, as this is a MFRC522 based clone.
